# Fritzing sketch Untitled Sketch (saved by Fritzing 1.0.3b)
breadboards: 1

parts:
  LED1 = RGB LED (com. cathode, rgb) [color="Red (633nm)" current=0.030A package="5 mm [THT]"]
  HC-SR04_Sensor_1 = HC-SR04 Ultrasonic Distance Sensor
  U1 = ESP32S-HiLetgo [part_number=ESP32S-HiLetgo]

nets:
  N1: LED1.red_anode, U1.GPIO5
  GND: LED1.common_cathode, HC-SR04_Sensor_1.GND, U1.GND
  N2: LED1.green_anode, U1.GPIO18
  N3: LED1.blue_anode, U1.GPIO19
  VCC: HC-SR04_Sensor_1.VCC, U1.VIN
  N4: HC-SR04_Sensor_1.TRIG, U1.GPIO23
  N5: HC-SR04_Sensor_1.ECHO, U1.GPIO22

custom parts:
  ESP32S-HiLetgo: HiLetgo ESP-WROOM-32 ESP32 ESP-32S Development Board 2.4GHz Dual-Mode WiFi + Bluetooth Dual Cores Microcontroller The ESP32 integrated with Antenna switches, RF Balun, power amplifiers, low-noise amplifiers, filters, and management modules, and the entire solution occupies the least area of PCB. 2.4 GHz Wi-Fi plus Bluetooth dual-mode chip, with TSMC Ultra-low power consumption 40nm technology,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
